// Digital circuit Processador acho.dig as structural Verilog
module Processador_acho (
  input  clock
);

  wire [1:0] register_1_q;
  wire [15:0] IP_q, multiplexer_1_out, reginaldos_1_p5, reginaldos_1_p6;
  wire [15:3] reginaldos_1_p1, reginaldos_1_p2, undriven;

  Register #(.Bits(16)) IP (.C(clock), .Q(IP_q));  // open: D, en
  Register register_1 (.C(clock), .Q(register_1_q[0]));  // open: D, en
  Multiplexer #(.Bits(16), .Selector_Bits(2)) multiplexer_1 (
    .sel(register_1_q), .in_0({reginaldos_1_p1, IP_q[11:9]}), .in_1({reginaldos_1_p2, IP_q[8:6]}),
    .in_2({undriven, IP_q[5:3]}), .out(multiplexer_1_out));  // open: in_3
  // Reginaldos reginaldos_1: pin names not known; wires that end beside it: {reginaldos_1_p1, IP_q[11:9]}, {reginaldos_1_p2, IP_q[8:6]}, multiplexer_1_out, clock, reginaldos_1_p5, reginaldos_1_p6
  Register #(.Bits(16)) ULAA (.D(reginaldos_1_p5), .C(clock));  // open: en, Q
  Register #(.Bits(16)) ULAB (.D(reginaldos_1_p6), .C(clock));  // open: en, Q
  // Pins of 3 and 16 bits meet at {undriven, IP_q[5:3]}
  // Pins of 3 and 16 bits meet at {reginaldos_1_p2, IP_q[8:6]}
  // Pins of 3 and 16 bits meet at {reginaldos_1_p1, IP_q[11:9]}
  // Pins of 1 and 2 bits meet at register_1_q
endmodule
